// Digital circuit 01-register-74HC173.dig as structural Verilog
module _01_register_74HC173 (
  input  OE,
  input  DE,
  input  RESET,
  input  clk,
  input  in_5,
  input  in_6,
  input  in_7,
  input  in_8,
  output out_9,
  output out_10,
  output out_11,
  output out_12
);

  wire not_1_out, not_2_out;

  not not_1 (not_1_out, OE);
  not not_2 (not_2_out, DE);
  _74173 _74173_1 (
    .pin1(not_1_out), .pin2(not_1_out), .pin3(out_9), .pin4(out_10), .pin5(out_11), .pin6(out_12),
    .pin7(clk), .pin8(1'b0), .pin9(not_2_out), .pin10(not_2_out), .pin11(in_8), .pin12(in_7), .pin13(in_6),
    .pin14(in_5), .pin15(RESET), .pin16(1'b1));

  // Notes on the sheet:
  //   OE: sadsadasf
endmodule
