// Digital circuit 03-icpu.dig as structural Verilog
module _03_icpu (
  input  CLOCK,
  input  in_2,
  input  in_3,
  input  in_4,
  input  in_5,
  input  in_6,
  input  in_7,
  input  in_8,
  input  in_9,
  input  in_10,
  input  BIE,
  input  BOE,
  input  AIE,
  input  AOE,
  input  RST,
  input  in_16,
  input  in_17,
  input  _0,
  input  _1,
  input  _2,
  input  _3,
  input  _4,
  input  _5,
  input  _6,
  input  _7
);

  wire AIE_t, AOE_t, BIE_t, BOE_t;

  _02_register _02_register_1 (
    .DE(AIE_t), .OE(AOE_t), .RST(RST), .D0(_0), .D1(_1), .D2(_2), .D3(_3), .CLK(CLOCK), .D4(_4), .D5(_5),
    .D6(_6), .D7(_7), .Q0(_0), .Q1(_1), .Q2(_2), .Q3(_3), .Q4(_4), .Q5(_5), .Q6(_6), .Q7(_7));
  LED u__7 (.in(_7));
  LED u__6 (.in(_6));
  LED u__5 (.in(_5));
  LED u__4 (.in(_4));
  LED u__3 (.in(_3));
  LED u__2 (.in(_2));
  LED u__1 (.in(_1));
  not not_1 (BOE_t, BOE);
  not not_2 (BIE_t, BIE);
  LED u__0 (.in(_0));
  not not_3 (AOE_t, AOE);
  not not_4 (AIE_t, AIE);
  _02_register _02_register_2 (
    .DE(BIE_t), .OE(BOE_t), .RST(RST), .D0(_0), .D1(_1), .D2(_2), .D3(_3), .CLK(CLOCK), .D4(_4), .D5(_5),
    .D6(_6), .D7(_7), .Q0(_0), .Q1(_1), .Q2(_2), .Q3(_3), .Q4(_4), .Q5(_5), .Q6(_6), .Q7(_7));

  // Other names for the same wires on the sheet: CLK = CLOCK

  // Notes on the sheet:
  //   Register A
  //   Register B
endmodule
