// Digital circuit 04-icpu-input.dig as structural Verilog
module _04_icpu_input (
  input  CLOCK,
  input  in_2,
  input  in_3,
  input  in_4,
  input  in_5,
  input  in_6,
  input  in_7,
  input  in_8,
  input  in_9,
  input  in_10,
  input  BIE,
  input  BOE,
  input  AIE,
  input  AOE,
  input  RST,
  input  IOE,
  input  in_17,
  input  _2,
  input  _3,
  input  _4,
  input  _5,
  input  _6,
  input  _7,
  input  _0,
  input  _1
);

  wire AIE_t, AOE_t, BIE_t, BOE_t, IOE_t;
  wire [3:0] _74245_1_pin12, _74245_1_pin17;

  not not_1 (IOE_t, IOE);
  _74245 _74245_1 (
    .pin1(1'b1), .pin2(_0), .pin3(_1), .pin4(_2), .pin5(_3), .pin6(_4), .pin7(_5), .pin8(_6), .pin9(_7),
    .pin10(1'b0), .pin11(_74245_1_pin12[3]), .pin12(_74245_1_pin12[2]), .pin13(_74245_1_pin12[1]),
    .pin14(_74245_1_pin12[0]), .pin15(_74245_1_pin17[3]), .pin16(_74245_1_pin17[2]),
    .pin17(_74245_1_pin17[1]), .pin18(_74245_1_pin17[0]), .pin19(IOE_t), .pin20(1'b1));
  _02_register _02_register_1 (
    .DE(AIE_t), .OE(AOE_t), .RST(RST), .D0(_74245_1_pin17[0]), .D1(_74245_1_pin17[1]),
    .D2(_74245_1_pin17[2]), .D3(_74245_1_pin17[3]), .CLK(CLOCK), .D4(_74245_1_pin12[0]),
    .D5(_74245_1_pin12[1]), .D6(_74245_1_pin12[2]), .D7(_74245_1_pin12[3]), .Q0(_74245_1_pin17[0]),
    .Q1(_74245_1_pin17[1]), .Q2(_74245_1_pin17[2]), .Q3(_74245_1_pin17[3]), .Q4(_74245_1_pin12[0]),
    .Q5(_74245_1_pin12[1]), .Q6(_74245_1_pin12[2]), .Q7(_74245_1_pin12[3]));
  LED u__7 (.in(_74245_1_pin12[3]));
  LED u__6 (.in(_74245_1_pin12[2]));
  LED u__5 (.in(_74245_1_pin12[1]));
  LED u__4 (.in(_74245_1_pin12[0]));
  LED u__3 (.in(_74245_1_pin17[3]));
  LED u__2 (.in(_74245_1_pin17[2]));
  LED u__1 (.in(_74245_1_pin17[1]));
  not not_2 (BOE_t, BOE);
  not not_3 (BIE_t, BIE);
  LED u__0 (.in(_74245_1_pin17[0]));
  not not_4 (AOE_t, AOE);
  not not_5 (AIE_t, AIE);
  Seven_Seg_Hex seven_seg_hex_1 (.d(_74245_1_pin12), .dp(1'b0));
  Seven_Seg_Hex seven_seg_hex_2 (.d(_74245_1_pin17), .dp(1'b0));
  _02_register _02_register_2 (
    .DE(BIE_t), .OE(BOE_t), .RST(RST), .D0(_74245_1_pin17[0]), .D1(_74245_1_pin17[1]),
    .D2(_74245_1_pin17[2]), .D3(_74245_1_pin17[3]), .CLK(CLOCK), .D4(_74245_1_pin12[0]),
    .D5(_74245_1_pin12[1]), .D6(_74245_1_pin12[2]), .D7(_74245_1_pin12[3]), .Q0(_74245_1_pin17[0]),
    .Q1(_74245_1_pin17[1]), .Q2(_74245_1_pin17[2]), .Q3(_74245_1_pin17[3]), .Q4(_74245_1_pin12[0]),
    .Q5(_74245_1_pin12[1]), .Q6(_74245_1_pin12[2]), .Q7(_74245_1_pin12[3]));

  // Other names for the same wires on the sheet: CLK = CLOCK

  // Notes on the sheet:
  //   Register A
  //   Register B
endmodule
