// Digital circuit 05-RAM-Addre-Demux.dig as structural Verilog
module _05_RAM_Addre_Demux (
  input  _3,
  input  _2,
  input  _1,
  input  _0
);

  wire nand_1_out, nand_2_out, notconnected_1_out, notconnected_3_out, notconnected_4_out,
       notconnected_5_out, notconnected_6_out, notconnected_7_out, notconnected_8_out, notconnected_9_out,
       notconnected_10_out, notconnected_11_out;

  nand nand_1 (nand_1_out, ~_0, ~_1, ~_2, ~_3);  // NAnd
  nand nand_2 (nand_2_out, _0, ~_1, ~_2, ~_3);  // NAnd
  // NotConnected on notconnected_1_out
  // NotConnected on nothing
  // NotConnected on notconnected_3_out
  // NotConnected on notconnected_4_out
  // NotConnected on notconnected_5_out
  // NotConnected on notconnected_6_out
  // NotConnected on notconnected_7_out
  // NotConnected on notconnected_8_out
  // NotConnected on notconnected_9_out
  // NotConnected on notconnected_10_out
  // NotConnected on notconnected_11_out
  // _02_register _0: pin names not known; wires that end beside it: nand_1_out, notconnected_1_out
  _02_register u__1 ();  // open: DE, OE, RST, D0, D1, D2, D3, CLK, D4, D5, D6, D7, Q0, Q1, Q2, Q3, Q4, Q5, Q6, Q7
  // _02_register _2: pin names not known; wires that end beside it: nand_2_out
  // _02_register _3: pin names not known; wires that end beside it: notconnected_3_out, notconnected_4_out, notconnected_5_out
  // _02_register _4: pin names not known; wires that end beside it: notconnected_6_out, notconnected_7_out
  _02_register _5 ();  // open: DE, OE, RST, D0, D1, D2, D3, CLK, D4, D5, D6, D7, Q0, Q1, Q2, Q3, Q4, Q5, Q6, Q7
  // _02_register _6: pin names not known; wires that end beside it: notconnected_8_out
  // _02_register _7: pin names not known; wires that end beside it: notconnected_9_out, notconnected_10_out, notconnected_11_out
endmodule
