// Digital circuit 06-8bit-counter.dig as structural Verilog
module _06_8bit_counter (
  input  D0,
  input  D1,
  input  D2,
  input  D3,
  input  D4,
  input  D5,
  input  D6,
  input  D7,
  input  RST,
  input  CE,
  input  JMP,
  input  CLK,
  output Q0,
  output ERR,
  output Q1,
  output Q2,
  output Q3,
  output Q4,
  output Q5,
  output Q6,
  output Q7
);

  wire _74161_1_pin15;

  _74161 _74161_1 (
    .pin1(RST), .pin2(CLK), .pin3(D0), .pin4(D1), .pin5(D2), .pin6(D3), .pin7(CE), .pin8(1'b0), .pin9(JMP),
    .pin10(CE), .pin11(Q3), .pin12(Q2), .pin13(Q1), .pin14(Q0), .pin15(_74161_1_pin15), .pin16(1'b1));
  _74161 _74161_2 (
    .pin1(RST), .pin2(CLK), .pin3(D4), .pin4(D5), .pin5(D6), .pin6(D7), .pin7(_74161_1_pin15), .pin8(1'b0),
    .pin9(JMP), .pin10(_74161_1_pin15), .pin11(Q7), .pin12(Q6), .pin13(Q5), .pin14(Q4), .pin15(ERR),
    .pin16(1'b1));
  Seven_Seg_Hex seven_seg_hex_1 (.d({Q7, Q6, Q5, Q4}), .dp(1'b0));
  Seven_Seg_Hex seven_seg_hex_2 (.d({Q3, Q2, Q1, Q0}), .dp(1'b0));

  // Notes on the sheet:
  //   CLK: Hz: 3
endmodule
