// Digital circuit 07-program-counter.dig as structural Verilog
module _07_program_counter (
  input  PCCE,
  input  D0,
  input  D1,
  input  D2,
  input  D3,
  input  D4,
  input  D5,
  input  D6,
  input  D7,
  input  RST,
  input  CLK,
  input  PCOE,
  input  JMP,
  output Q0,
  output Q1,
  output Q2,
  output Q3,
  output Q4,
  output Q5,
  output Q6,
  output Q7,
  output ERR
);

  wire _74161_1_pin11, _74161_1_pin12, _74161_1_pin13, _74161_1_pin14, _74161_1_pin15, _74161_2_pin11,
       _74161_2_pin12, _74161_2_pin13, _74161_2_pin14;

  _74161 _74161_1 (
    .pin1(RST), .pin2(CLK), .pin3(D0), .pin4(D1), .pin5(D2), .pin6(D3), .pin7(PCCE), .pin8(1'b0), .pin9(JMP),
    .pin10(PCCE), .pin11(_74161_1_pin11), .pin12(_74161_1_pin12), .pin13(_74161_1_pin13),
    .pin14(_74161_1_pin14), .pin15(_74161_1_pin15), .pin16(1'b1));
  _74161 _74161_2 (
    .pin1(RST), .pin2(CLK), .pin3(D4), .pin4(D5), .pin5(D6), .pin6(D7), .pin7(_74161_1_pin15), .pin8(1'b0),
    .pin9(JMP), .pin10(_74161_1_pin15), .pin11(_74161_2_pin11), .pin12(_74161_2_pin12),
    .pin13(_74161_2_pin13), .pin14(_74161_2_pin14), .pin15(ERR), .pin16(1'b1));
  _74245 _74245_1 (
    .pin1(1'b1), .pin2(_74161_1_pin14), .pin3(_74161_1_pin13), .pin4(_74161_1_pin12), .pin5(_74161_1_pin11),
    .pin6(_74161_2_pin14), .pin7(_74161_2_pin13), .pin8(_74161_2_pin12), .pin9(_74161_2_pin11), .pin10(1'b0),
    .pin11(Q7), .pin12(Q6), .pin13(Q5), .pin14(Q4), .pin15(Q3), .pin16(Q2), .pin17(Q1), .pin18(Q0),
    .pin19(PCOE), .pin20(1'b1));

  // Notes on the sheet:
  //   PCCE: pin 1
  //   D0: pin 2
  //   D1: pin 3
  //   D2: pin 4
  //   D3: pin 5
  //   D4: pin 6
  //   D5: pin 7
  //   D6: pin 8
  //   Q0: pin 13
  //   Q1: pin 14
  //   D7: pin 9
  //   RST: pin 10
  //   CLK: pin 11
  //   Q2: pin 15
  //   Q3: pin 16
  //   Q4: pin 17
  //   Q5: pin 18
  //   Q6: pin 19
  //   Q7: pin 20
  //   ERR: pin 22
  //   PCOE: pin 12
  //   JMP: pin 21
endmodule
