// Digital circuit 08-icpu-pc.dig as structural Verilog
module _08_icpu_pc (
  input  CLOCK,
  input  ROE,
  input  RAIE,
  input  PCOE,
  input  PCCE,
  input  JMP,
  input  in_7,
  input  in_8,
  input  in_9,
  input  in_10,
  input  BIE,
  input  BOE,
  input  AIE,
  input  AOE,
  input  RST,
  input  IOE,
  input  RWE,
  input  _2,
  input  _3,
  input  _4,
  input  _5,
  input  _6,
  input  _7,
  input  _0,
  input  _1
);

  wire AIE_t, AOE_t, BIE_t, BOE_t, ERR, IOE_t, JMP_t, nor_1_out, PCOE_t, RAIE_t, ROE_t, RST_t, RWE_t;
  wire [3:0] _74245_1_pin11, _74245_1_pin16;
  wire [7:0] _02_register_3_q0, ramsingleportsel_1_d;

  _74245 _74245_1 (
    .pin1(1'b1), .pin2(_0), .pin3(_1), .pin4(_2), .pin5(_3), .pin6(_4), .pin7(_5), .pin8(_6), .pin9(_7),
    .pin10(1'b0), .pin11(_74245_1_pin11[3]), .pin12(_74245_1_pin11[2]), .pin13(_74245_1_pin11[1]),
    .pin14(_74245_1_pin11[0]), .pin15(_74245_1_pin16[3]), .pin16(_74245_1_pin16[2]),
    .pin17(_74245_1_pin16[1]), .pin18(_74245_1_pin16[0]), .pin19(IOE_t), .pin20(1'b1));
  not not_1 (IOE_t, IOE);
  not not_2 (RWE_t, RWE);
  not not_3 (RAIE_t, RAIE);
  _02_register _02_register_1 (
    .DE(AIE_t), .OE(AOE_t), .RST(RST), .D0(_74245_1_pin16[0]), .D1(_74245_1_pin16[1]),
    .D2(_74245_1_pin16[2]), .D3(_74245_1_pin16[3]), .CLK(CLOCK), .D4(_74245_1_pin11[0]),
    .D5(_74245_1_pin11[1]), .D6(_74245_1_pin11[2]), .D7(_74245_1_pin11[3]), .Q0(_74245_1_pin16[0]),
    .Q1(_74245_1_pin16[1]), .Q2(_74245_1_pin16[2]), .Q3(_74245_1_pin16[3]), .Q4(_74245_1_pin11[0]),
    .Q5(_74245_1_pin11[1]), .Q6(_74245_1_pin11[2]), .Q7(_74245_1_pin11[3]));
  _07_program_counter _07_program_counter_1 (
    .PCCE(PCCE), .D0(_74245_1_pin16[0]), .D1(_74245_1_pin16[1]), .D2(_74245_1_pin16[2]),
    .D3(_74245_1_pin16[3]), .D4(_74245_1_pin11[0]), .D5(_74245_1_pin11[1]), .D6(_74245_1_pin11[2]),
    .Q0(_74245_1_pin16[0]), .Q1(_74245_1_pin16[1]), .D7(_74245_1_pin11[3]), .RST(RST_t), .CLK(CLOCK),
    .Q2(_74245_1_pin16[2]), .Q3(_74245_1_pin16[3]), .Q4(_74245_1_pin11[0]), .Q5(_74245_1_pin11[1]),
    .Q6(_74245_1_pin11[2]), .Q7(_74245_1_pin11[3]), .ERR(ERR), .PCOE(PCOE_t), .JMP(JMP_t));
  not not_4 (ROE_t, ROE);
  not not_5 (PCOE_t, PCOE);
  LED u__7 (.in(_74245_1_pin11[3]));
  not not_6 (JMP_t, JMP);
  LED u__6 (.in(_74245_1_pin11[2]));
  LED u__5 (.in(_74245_1_pin11[1]));
  LED u__4 (.in(_74245_1_pin11[0]));
  LED u__3 (.in(_74245_1_pin16[3]));
  LED u__2 (.in(_74245_1_pin16[2]));
  LED u__1 (.in(_74245_1_pin16[1]));
  not not_7 (BOE_t, BOE);
  not not_8 (BIE_t, BIE);
  LED u__0 (.in(_74245_1_pin16[0]));
  not not_9 (AOE_t, AOE);
  not not_10 (AIE_t, AIE);
  Seven_Seg_Hex seven_seg_hex_1 (.d(_74245_1_pin11), .dp(1'b0));
  Seven_Seg_Hex seven_seg_hex_2 (.d(_74245_1_pin16), .dp(1'b0));
  _02_register _02_register_2 (
    .DE(BIE_t), .OE(BOE_t), .RST(RST), .D0(_74245_1_pin16[0]), .D1(_74245_1_pin16[1]),
    .D2(_74245_1_pin16[2]), .D3(_74245_1_pin16[3]), .CLK(CLOCK), .D4(_74245_1_pin11[0]),
    .D5(_74245_1_pin11[1]), .D6(_74245_1_pin11[2]), .D7(_74245_1_pin11[3]), .Q0(_74245_1_pin16[0]),
    .Q1(_74245_1_pin16[1]), .Q2(_74245_1_pin16[2]), .Q3(_74245_1_pin16[3]), .Q4(_74245_1_pin11[0]),
    .Q5(_74245_1_pin11[1]), .Q6(_74245_1_pin11[2]), .Q7(_74245_1_pin11[3]));
  _02_register _02_register_3 (
    .DE(RAIE_t), .OE(1'b0), .RST(RST), .D0(_74245_1_pin16[0]), .D1(_74245_1_pin16[1]),
    .D2(_74245_1_pin16[2]), .D3(_74245_1_pin16[3]), .CLK(CLOCK), .D4(_74245_1_pin11[0]),
    .D5(_74245_1_pin11[1]), .D6(_74245_1_pin11[2]), .D7(_74245_1_pin11[3]), .Q0(_02_register_3_q0[0]),
    .Q1(_02_register_3_q0[1]), .Q2(_02_register_3_q0[2]), .Q3(_02_register_3_q0[3]),
    .Q4(_02_register_3_q0[4]), .Q5(_02_register_3_q0[5]), .Q6(_02_register_3_q0[6]), .Q7(_02_register_3_q0[7]));
  not not_11 (RST_t, RST);
  LED u_ERR (.in(ERR));
  nor nor_1 (nor_1_out, 1'b0, ~RWE_t, ROE_t);  // NOr
  RAMSinglePortSel #(.AddrBits(8), .Bits(8)) ramsingleportsel_1 (
    .A(_02_register_3_q0), .CS(~1'b0), .WE(~RWE_t), .OE(~ROE_t), .D(ramsingleportsel_1_d));
  BusSplitter #(.Bits(8)) bussplitter_1 (
    .D(ramsingleportsel_1_d), .OE(nor_1_out), .D0(_74245_1_pin16[0]), .D1(_74245_1_pin16[1]),
    .D2(_74245_1_pin16[2]), .D3(_74245_1_pin16[3]), .D4(_74245_1_pin11[0]), .D5(_74245_1_pin11[1]),
    .D6(_74245_1_pin11[2]), .D7(_74245_1_pin11[3]));

  // Other names for the same wires on the sheet: CLK = CLOCK

  // Notes on the sheet:
  //   CLOCK: Hz: 2
  //   Input
  //   Program Counter
  //   Register A
  //   RAM
  //   Register B
endmodule
