// Digital circuit 09-icpu-ir.dig as structural Verilog
module _09_icpu_ir (
  input  CLOCK,
  input  RO,
  input  MI,
  input  CO,
  input  CE,
  input  JUMP,
  input  CODEI,
  input  RANDI,
  input  RANDO,
  input  in_10,
  input  BI,
  input  BO,
  input  AI,
  input  AO,
  input  RST,
  input  IO,
  input  RW,
  input  _2,
  input  _3,
  input  _4,
  input  _5,
  input  _6,
  input  _7,
  input  _0,
  input  _1,
  input  in_26
);

  wire AIE, AOE, BIE, BOE, ERR, IOE, IRCI, IRO, IRRI, JMP, nor_1_out, PCOE, RAIE, ROE, RST_t, RWE;
  wire [3:0] _02_register_2_q0, _02_register_2_q7;
  wire [7:0] _02_register_5_q0, DEBUG_IROPCODE, ramsingleportsel_1_d;

  _02_register _02_register_1 (
    .DE(IRCI), .OE(1'b0), .RST(RST), .D0(_02_register_2_q0[0]), .D1(_02_register_2_q0[1]),
    .D2(_02_register_2_q0[2]), .D3(_02_register_2_q0[3]), .CLK(CLOCK), .D4(_02_register_2_q7[0]),
    .D5(_02_register_2_q7[1]), .D6(_02_register_2_q7[2]), .D7(_02_register_2_q7[3]), .Q0(DEBUG_IROPCODE[0]),
    .Q1(DEBUG_IROPCODE[1]), .Q2(DEBUG_IROPCODE[2]), .Q3(DEBUG_IROPCODE[3]), .Q4(DEBUG_IROPCODE[4]),
    .Q5(DEBUG_IROPCODE[5]), .Q6(DEBUG_IROPCODE[6]), .Q7(DEBUG_IROPCODE[7]));
  _02_register _02_register_2 (
    .DE(IRRI), .OE(IRO), .RST(RST), .D0(_02_register_2_q0[0]), .D1(_02_register_2_q0[1]),
    .D2(_02_register_2_q0[2]), .D3(_02_register_2_q0[3]), .CLK(CLOCK), .D4(_02_register_2_q7[0]),
    .D5(_02_register_2_q7[1]), .D6(_02_register_2_q7[2]), .D7(_02_register_2_q7[3]),
    .Q0(_02_register_2_q0[0]), .Q1(_02_register_2_q0[1]), .Q2(_02_register_2_q0[2]),
    .Q3(_02_register_2_q0[3]), .Q4(_02_register_2_q7[0]), .Q5(_02_register_2_q7[1]),
    .Q6(_02_register_2_q7[2]), .Q7(_02_register_2_q7[3]));
  _74245 _74245_1 (
    .pin1(1'b1), .pin2(_0), .pin3(_1), .pin4(_2), .pin5(_3), .pin6(_4), .pin7(_5), .pin8(_6), .pin9(_7),
    .pin10(1'b0), .pin11(_02_register_2_q7[3]), .pin12(_02_register_2_q7[2]), .pin13(_02_register_2_q7[1]),
    .pin14(_02_register_2_q7[0]), .pin15(_02_register_2_q0[3]), .pin16(_02_register_2_q0[2]),
    .pin17(_02_register_2_q0[1]), .pin18(_02_register_2_q0[0]), .pin19(IOE), .pin20(1'b1));
  not not_1 (IOE, IO);
  not not_2 (RWE, RW);
  not not_3 (RAIE, MI);
  _02_register _02_register_3 (
    .DE(AIE), .OE(AOE), .RST(RST), .D0(_02_register_2_q0[0]), .D1(_02_register_2_q0[1]),
    .D2(_02_register_2_q0[2]), .D3(_02_register_2_q0[3]), .CLK(CLOCK), .D4(_02_register_2_q7[0]),
    .D5(_02_register_2_q7[1]), .D6(_02_register_2_q7[2]), .D7(_02_register_2_q7[3]),
    .Q0(_02_register_2_q0[0]), .Q1(_02_register_2_q0[1]), .Q2(_02_register_2_q0[2]),
    .Q3(_02_register_2_q0[3]), .Q4(_02_register_2_q7[0]), .Q5(_02_register_2_q7[1]),
    .Q6(_02_register_2_q7[2]), .Q7(_02_register_2_q7[3]));
  _07_program_counter _07_program_counter_1 (
    .PCCE(CE), .D0(_02_register_2_q0[0]), .D1(_02_register_2_q0[1]), .D2(_02_register_2_q0[2]),
    .D3(_02_register_2_q0[3]), .D4(_02_register_2_q7[0]), .D5(_02_register_2_q7[1]),
    .D6(_02_register_2_q7[2]), .Q0(_02_register_2_q0[0]), .Q1(_02_register_2_q0[1]),
    .D7(_02_register_2_q7[3]), .RST(RST_t), .CLK(CLOCK), .Q2(_02_register_2_q0[2]),
    .Q3(_02_register_2_q0[3]), .Q4(_02_register_2_q7[0]), .Q5(_02_register_2_q7[1]),
    .Q6(_02_register_2_q7[2]), .Q7(_02_register_2_q7[3]), .ERR(ERR), .PCOE(PCOE), .JMP(JMP));
  not not_4 (ROE, RO);
  not not_5 (PCOE, CO);
  LED u__7 (.in(_02_register_2_q7[3]));
  not not_6 (JMP, JUMP);
  LED u__6 (.in(_02_register_2_q7[2]));
  LED u__5 (.in(_02_register_2_q7[1]));
  not not_7 (IRCI, CODEI);
  not not_8 (IRRI, RANDI);
  LED u__4 (.in(_02_register_2_q7[0]));
  LED u__3 (.in(_02_register_2_q0[3]));
  not not_9 (IRO, RANDO);
  LED u__2 (.in(_02_register_2_q0[2]));
  LED u__1 (.in(_02_register_2_q0[1]));
  not not_10 (BIE, BI);
  LED u__0 (.in(_02_register_2_q0[0]));
  not not_11 (AIE, AI);
  not not_12 (BOE, BO);
  Seven_Seg_Hex seven_seg_hex_1 (.d(_02_register_2_q7), .dp(1'b0));
  not not_13 (AOE, AO);
  Seven_Seg_Hex seven_seg_hex_2 (.d(_02_register_2_q0), .dp(1'b0));
  _02_register _02_register_4 (
    .DE(BIE), .OE(BOE), .RST(RST), .D0(_02_register_2_q0[0]), .D1(_02_register_2_q0[1]),
    .D2(_02_register_2_q0[2]), .D3(_02_register_2_q0[3]), .CLK(CLOCK), .D4(_02_register_2_q7[0]),
    .D5(_02_register_2_q7[1]), .D6(_02_register_2_q7[2]), .D7(_02_register_2_q7[3]),
    .Q0(_02_register_2_q0[0]), .Q1(_02_register_2_q0[1]), .Q2(_02_register_2_q0[2]),
    .Q3(_02_register_2_q0[3]), .Q4(_02_register_2_q7[0]), .Q5(_02_register_2_q7[1]),
    .Q6(_02_register_2_q7[2]), .Q7(_02_register_2_q7[3]));
  _02_register _02_register_5 (
    .DE(RAIE), .OE(1'b0), .RST(RST), .D0(_02_register_2_q0[0]), .D1(_02_register_2_q0[1]),
    .D2(_02_register_2_q0[2]), .D3(_02_register_2_q0[3]), .CLK(CLOCK), .D4(_02_register_2_q7[0]),
    .D5(_02_register_2_q7[1]), .D6(_02_register_2_q7[2]), .D7(_02_register_2_q7[3]),
    .Q0(_02_register_5_q0[0]), .Q1(_02_register_5_q0[1]), .Q2(_02_register_5_q0[2]),
    .Q3(_02_register_5_q0[3]), .Q4(_02_register_5_q0[4]), .Q5(_02_register_5_q0[5]),
    .Q6(_02_register_5_q0[6]), .Q7(_02_register_5_q0[7]));
  not not_14 (RST_t, RST);
  LED u_ERR (.in(ERR));
  nor nor_1 (nor_1_out, 1'b0, ~RWE, ROE);  // NOr
  Seven_Seg_Hex seven_seg_hex_3 (.d(DEBUG_IROPCODE[7:4]), .dp(1'b0));
  RAMSinglePortSel #(.AddrBits(8), .Bits(8)) ramsingleportsel_1 (
    .A(_02_register_5_q0), .CS(~1'b0), .WE(~RWE), .OE(~ROE), .D(ramsingleportsel_1_d));
  Seven_Seg_Hex seven_seg_hex_4 (.d(DEBUG_IROPCODE[3:0]), .dp(1'b0));
  Seven_Seg_Hex seven_seg_hex_5 (.dp(DEBUG_IROPCODE[4]));  // open: d
  BusSplitter #(.Bits(8)) bussplitter_1 (
    .D(ramsingleportsel_1_d), .OE(nor_1_out), .D0(_02_register_2_q0[0]), .D1(_02_register_2_q0[1]),
    .D2(_02_register_2_q0[2]), .D3(_02_register_2_q0[3]), .D4(_02_register_2_q7[0]),
    .D5(_02_register_2_q7[1]), .D6(_02_register_2_q7[2]), .D7(_02_register_2_q7[3]));
  Seven_Seg_Hex seven_seg_hex_6 (.d(DEBUG_IROPCODE[3:0]), .dp(1'b0));
  // Pins of 1 and 4 bits meet at DEBUG_IROPCODE[7:4]
  // also tied to GND on the sheet: DEBUG_IROPCODE[4]

  // Other names for the same wires on the sheet: CLK = CLOCK; PCCE = CE

  // Notes on the sheet:
  //   CLOCK: Hz: 2
  //   Input
  //   Program Counter
  //   Register A
  //   RAM
  //   Register B
endmodule
