// Digital circuit 10-icpu-controller-1.dig as structural Verilog
module _10_icpu_controller_1 (
  input  CLOCK,
  input  RST,
  input  _2,
  input  _3,
  input  _4,
  input  _5,
  input  _6,
  input  _7,
  input  _0,
  input  _1
);

  wire _74161_1_pin2, _74161_1_pin3, _74161_1_pin4, _74161_1_pin5, _74161_1_pin6, AI, AIE, AO, AOE, BI, BIE,
       BO, BOE, CE, CO, CODEI, ERR, IO, IOE, IRCI, IRO, IRRI, JMP, JUMP, MI, nor_1_out, PCOE, RAIE, RANDI,
       RANDO, RO, ROE, RST_t, RW, RWE;
  wire [1:0] eeprom_1_d;
  wire [3:0] _74161_1_pin14;
  wire [7:0] _02_register_5_q0, DEBUG_IROPCODE, DEBUG_IROPRAND, ramsingleportsel_1_d;

  _74161 _74161_1 (
    .pin1(1'b1), .pin2(_74161_1_pin2), .pin3(_74161_1_pin3), .pin4(_74161_1_pin4), .pin5(_74161_1_pin5),
    .pin6(_74161_1_pin6), .pin7(1'b1), .pin8(1'b0), .pin9(1'b1), .pin10(1'b1), .pin11(_74161_1_pin14[3]),
    .pin12(_74161_1_pin14[2]), .pin13(_74161_1_pin14[1]), .pin14(_74161_1_pin14[0]), .pin16(1'b1));  // open: pin15
  not not_1 (_74161_1_pin2, CLOCK);
  // NotConnected on _74161_1_pin3
  // NotConnected on _74161_1_pin4
  // NotConnected on _74161_1_pin5
  // NotConnected on _74161_1_pin6
  Seven_Seg_Hex seven_seg_hex_1 (.d({IO, MI, RW, RO}), .dp(1'b0));
  EEPROM #(.AddrBits(4), .Bits(16)) eeprom_1 (
    .A(_74161_1_pin14), .CS(~1'b0), .WE(~1'b1), .OE(~1'b0),
    .D({IO, MI, RW, RO, CO, CE, JUMP, CODEI, RANDI, RANDO, eeprom_1_d, BI, BO, AI, AO}));
  Seven_Seg_Hex seven_seg_hex_2 (.d({CO, CE, JUMP, CODEI}), .dp(1'b0));
  Seven_Seg_Hex seven_seg_hex_3 (.d({RANDI, RANDO, eeprom_1_d}), .dp(1'b0));
  Seven_Seg_Hex seven_seg_hex_4 (.d({BI, BO, AI, AO}), .dp(1'b0));
  LED led_1 (.in(eeprom_1_d[1]));
  LED led_2 (.in(eeprom_1_d[0]));
  _02_register _02_register_1 (
    .DE(IRCI), .OE(1'b0), .RST(RST), .D0(DEBUG_IROPRAND[0]), .D1(DEBUG_IROPRAND[1]), .D2(DEBUG_IROPRAND[2]),
    .D3(DEBUG_IROPRAND[3]), .CLK(CLOCK), .D4(DEBUG_IROPRAND[4]), .D5(DEBUG_IROPRAND[5]),
    .D6(DEBUG_IROPRAND[6]), .D7(DEBUG_IROPRAND[7]), .Q0(DEBUG_IROPCODE[0]), .Q1(DEBUG_IROPCODE[1]),
    .Q2(DEBUG_IROPCODE[2]), .Q3(DEBUG_IROPCODE[3]), .Q4(DEBUG_IROPCODE[4]), .Q5(DEBUG_IROPCODE[5]),
    .Q6(DEBUG_IROPCODE[6]), .Q7(DEBUG_IROPCODE[7]));
  _02_register _02_register_2 (
    .DE(IRRI), .OE(IRO), .RST(RST), .D0(DEBUG_IROPRAND[0]), .D1(DEBUG_IROPRAND[1]), .D2(DEBUG_IROPRAND[2]),
    .D3(DEBUG_IROPRAND[3]), .CLK(CLOCK), .D4(DEBUG_IROPRAND[4]), .D5(DEBUG_IROPRAND[5]),
    .D6(DEBUG_IROPRAND[6]), .D7(DEBUG_IROPRAND[7]), .Q0(DEBUG_IROPRAND[0]), .Q1(DEBUG_IROPRAND[1]),
    .Q2(DEBUG_IROPRAND[2]), .Q3(DEBUG_IROPRAND[3]), .Q4(DEBUG_IROPRAND[4]), .Q5(DEBUG_IROPRAND[5]),
    .Q6(DEBUG_IROPRAND[6]), .Q7(DEBUG_IROPRAND[7]));
  _74245 _74245_1 (
    .pin1(1'b1), .pin2(_0), .pin3(_1), .pin4(_2), .pin5(_3), .pin6(_4), .pin7(_5), .pin8(_6), .pin9(_7),
    .pin10(1'b0), .pin11(DEBUG_IROPRAND[7]), .pin12(DEBUG_IROPRAND[6]), .pin13(DEBUG_IROPRAND[5]),
    .pin14(DEBUG_IROPRAND[4]), .pin15(DEBUG_IROPRAND[3]), .pin16(DEBUG_IROPRAND[2]),
    .pin17(DEBUG_IROPRAND[1]), .pin18(DEBUG_IROPRAND[0]), .pin19(IOE), .pin20(1'b1));
  not not_2 (IOE, IO);
  not not_3 (RWE, RW);
  not not_4 (RAIE, MI);
  _02_register _02_register_3 (
    .DE(AIE), .OE(AOE), .RST(RST), .D0(DEBUG_IROPRAND[0]), .D1(DEBUG_IROPRAND[1]), .D2(DEBUG_IROPRAND[2]),
    .D3(DEBUG_IROPRAND[3]), .CLK(CLOCK), .D4(DEBUG_IROPRAND[4]), .D5(DEBUG_IROPRAND[5]),
    .D6(DEBUG_IROPRAND[6]), .D7(DEBUG_IROPRAND[7]), .Q0(DEBUG_IROPRAND[0]), .Q1(DEBUG_IROPRAND[1]),
    .Q2(DEBUG_IROPRAND[2]), .Q3(DEBUG_IROPRAND[3]), .Q4(DEBUG_IROPRAND[4]), .Q5(DEBUG_IROPRAND[5]),
    .Q6(DEBUG_IROPRAND[6]), .Q7(DEBUG_IROPRAND[7]));
  _07_program_counter _07_program_counter_1 (
    .PCCE(CE), .D0(DEBUG_IROPRAND[0]), .D1(DEBUG_IROPRAND[1]), .D2(DEBUG_IROPRAND[2]),
    .D3(DEBUG_IROPRAND[3]), .D4(DEBUG_IROPRAND[4]), .D5(DEBUG_IROPRAND[5]), .D6(DEBUG_IROPRAND[6]),
    .Q0(DEBUG_IROPRAND[0]), .Q1(DEBUG_IROPRAND[1]), .D7(DEBUG_IROPRAND[7]), .RST(RST_t), .CLK(CLOCK),
    .Q2(DEBUG_IROPRAND[2]), .Q3(DEBUG_IROPRAND[3]), .Q4(DEBUG_IROPRAND[4]), .Q5(DEBUG_IROPRAND[5]),
    .Q6(DEBUG_IROPRAND[6]), .Q7(DEBUG_IROPRAND[7]), .ERR(ERR), .PCOE(PCOE), .JMP(JMP));
  not not_5 (ROE, RO);
  not not_6 (PCOE, CO);
  LED u__7 (.in(DEBUG_IROPRAND[7]));
  not not_7 (JMP, JUMP);
  LED u__6 (.in(DEBUG_IROPRAND[6]));
  LED u__5 (.in(DEBUG_IROPRAND[5]));
  not not_8 (IRCI, CODEI);
  not not_9 (IRRI, RANDI);
  LED u__4 (.in(DEBUG_IROPRAND[4]));
  LED u__3 (.in(DEBUG_IROPRAND[3]));
  not not_10 (IRO, RANDO);
  LED u__2 (.in(DEBUG_IROPRAND[2]));
  LED u__1 (.in(DEBUG_IROPRAND[1]));
  not not_11 (BIE, BI);
  LED u__0 (.in(DEBUG_IROPRAND[0]));
  not not_12 (AIE, AI);
  not not_13 (BOE, BO);
  Seven_Seg_Hex seven_seg_hex_5 (.d(DEBUG_IROPRAND[7:4]), .dp(1'b0));
  not not_14 (AOE, AO);
  Seven_Seg_Hex seven_seg_hex_6 (.d(DEBUG_IROPRAND[3:0]), .dp(1'b0));
  _02_register _02_register_4 (
    .DE(BIE), .OE(BOE), .RST(RST), .D0(DEBUG_IROPRAND[0]), .D1(DEBUG_IROPRAND[1]), .D2(DEBUG_IROPRAND[2]),
    .D3(DEBUG_IROPRAND[3]), .CLK(CLOCK), .D4(DEBUG_IROPRAND[4]), .D5(DEBUG_IROPRAND[5]),
    .D6(DEBUG_IROPRAND[6]), .D7(DEBUG_IROPRAND[7]), .Q0(DEBUG_IROPRAND[0]), .Q1(DEBUG_IROPRAND[1]),
    .Q2(DEBUG_IROPRAND[2]), .Q3(DEBUG_IROPRAND[3]), .Q4(DEBUG_IROPRAND[4]), .Q5(DEBUG_IROPRAND[5]),
    .Q6(DEBUG_IROPRAND[6]), .Q7(DEBUG_IROPRAND[7]));
  _02_register _02_register_5 (
    .DE(RAIE), .OE(1'b0), .RST(RST), .D0(DEBUG_IROPRAND[0]), .D1(DEBUG_IROPRAND[1]), .D2(DEBUG_IROPRAND[2]),
    .D3(DEBUG_IROPRAND[3]), .CLK(CLOCK), .D4(DEBUG_IROPRAND[4]), .D5(DEBUG_IROPRAND[5]),
    .D6(DEBUG_IROPRAND[6]), .D7(DEBUG_IROPRAND[7]), .Q0(_02_register_5_q0[0]), .Q1(_02_register_5_q0[1]),
    .Q2(_02_register_5_q0[2]), .Q3(_02_register_5_q0[3]), .Q4(_02_register_5_q0[4]),
    .Q5(_02_register_5_q0[5]), .Q6(_02_register_5_q0[6]), .Q7(_02_register_5_q0[7]));
  not not_15 (RST_t, RST);
  LED u_ERR (.in(ERR));
  nor nor_1 (nor_1_out, 1'b0, ~RWE, ROE);  // NOr
  Seven_Seg_Hex seven_seg_hex_7 (.d(DEBUG_IROPCODE[7:4]), .dp(1'b0));
  RAMSinglePortSel #(.AddrBits(8), .Bits(8)) ramsingleportsel_1 (
    .A(_02_register_5_q0), .CS(~1'b0), .WE(~RWE), .OE(~ROE), .D(ramsingleportsel_1_d));
  Seven_Seg_Hex seven_seg_hex_8 (.d(DEBUG_IROPCODE[3:0]), .dp(1'b0));
  Seven_Seg_Hex seven_seg_hex_9 (.d(DEBUG_IROPRAND[7:4]), .dp(1'b0));
  BusSplitter #(.Bits(8)) bussplitter_1 (
    .D(ramsingleportsel_1_d), .OE(nor_1_out), .D0(DEBUG_IROPRAND[0]), .D1(DEBUG_IROPRAND[1]),
    .D2(DEBUG_IROPRAND[2]), .D3(DEBUG_IROPRAND[3]), .D4(DEBUG_IROPRAND[4]), .D5(DEBUG_IROPRAND[5]),
    .D6(DEBUG_IROPRAND[6]), .D7(DEBUG_IROPRAND[7]));
  Seven_Seg_Hex seven_seg_hex_10 (.d(DEBUG_IROPRAND[3:0]), .dp(1'b0));

  // Other names for the same wires on the sheet: PCCE = CE; CLK = CLOCK

  // Notes on the sheet:
  //   CLOCK: Hz: 2
  //   contents of eeprom_1 (hex, n*v repeats v):
  //   c000,c00,c0,c,1,10,100,1000,8000,800,80,8,0,0,0,c000
  //   Input
  //   Program Counter
  //   Register A
  //   RAM
  //   Register B
endmodule
