// Digital circuit 12-icpu-controller-3.dig as structural Verilog
module _12_icpu_controller_3 (
  input  CLOCK,
  input  RST,
  input  _2,
  input  _3,
  input  _4,
  input  _5,
  input  _6,
  input  _7,
  input  _0,
  input  _1
);

  wire _74161_1_pin2, _74161_1_pin3, _74161_1_pin4, _74161_1_pin5, _74161_1_pin6, AI, AIE, AO, AOE, BI, BIE,
       BO, BOE, BUS_0, BUS_1, BUS_2, BUS_3, BUS_4, BUS_5, BUS_6, BUS_7, CE, CO, CODEI, ERR, IO, IOE, IRCI,
       IRO, IRRI, JMP, JUMP, MI, nor_1_out, PCOE, RAIE, RANDI, RANDO, reset_1_out, RO, ROE, RST_t, RST_t_t,
       RW, RWE;
  wire [1:0] eeprom_1_d;
  wire [3:0] _74161_1_pin14;
  wire [7:0] _02_register_5_q0, DEBUG_IROPCODE, ramsingleportsel_1_d;

  _74161 _74161_1 (
    .pin1(1'b1), .pin2(_74161_1_pin2), .pin3(_74161_1_pin3), .pin4(_74161_1_pin4), .pin5(_74161_1_pin5),
    .pin6(_74161_1_pin6), .pin7(1'b1), .pin8(1'b0), .pin9(1'b1), .pin10(1'b1), .pin11(_74161_1_pin14[3]),
    .pin12(_74161_1_pin14[2]), .pin13(_74161_1_pin14[1]), .pin14(_74161_1_pin14[0]), .pin16(1'b1));  // open: pin15
  not not_1 (_74161_1_pin2, CLOCK);
  // NotConnected on _74161_1_pin3
  // NotConnected on _74161_1_pin4
  // NotConnected on _74161_1_pin5
  // NotConnected on _74161_1_pin6
  not not_2 (RST_t_t, RST_t);
  Reset #(.invertOutput("false")) reset_1 (.out(reset_1_out));
  or or_1 (RST_t, reset_1_out, RST);
  Seven_Seg_Hex seven_seg_hex_1 (.d({IO, MI, RW, RO}), .dp(1'b0));
  EEPROM #(.AddrBits(12), .Bits(16)) eeprom_1 (
    .A({DEBUG_IROPCODE, _74161_1_pin14}), .CS(~1'b0), .WE(~1'b1), .OE(~1'b0),
    .D({IO, MI, RW, RO, CO, CE, JUMP, CODEI, RANDI, RANDO, eeprom_1_d, BI, BO, AI, AO}));
  Seven_Seg_Hex seven_seg_hex_2 (.d({CO, CE, JUMP, CODEI}), .dp(1'b0));
  Seven_Seg_Hex seven_seg_hex_3 (.d({RANDI, RANDO, eeprom_1_d}), .dp(1'b0));
  Seven_Seg_Hex seven_seg_hex_4 (.d({BUS_7, BUS_6, BUS_5, BUS_4}), .dp(1'b0));
  Seven_Seg_Hex seven_seg_hex_5 (.d({BI, BO, AI, AO}), .dp(1'b0));
  LED led_1 (.in(eeprom_1_d[1]));
  LED led_2 (.in(eeprom_1_d[0]));
  Seven_Seg_Hex seven_seg_hex_6 (.d({BUS_3, BUS_2, BUS_1, BUS_0}), .dp(1'b0));
  _02_register _02_register_1 (
    .DE(IRCI), .OE(1'b0), .RST(RST_t), .D0(BUS_0), .D1(BUS_1), .D2(BUS_2), .D3(BUS_3), .CLK(CLOCK),
    .D4(BUS_4), .D5(BUS_5), .D6(BUS_6), .D7(BUS_7), .Q0(DEBUG_IROPCODE[0]), .Q1(DEBUG_IROPCODE[1]),
    .Q2(DEBUG_IROPCODE[2]), .Q3(DEBUG_IROPCODE[3]), .Q4(DEBUG_IROPCODE[4]), .Q5(DEBUG_IROPCODE[5]),
    .Q6(DEBUG_IROPCODE[6]), .Q7(DEBUG_IROPCODE[7]));
  LED u_ERR (.in(ERR));
  Seven_Seg_Hex seven_seg_hex_7 (.d(DEBUG_IROPCODE[7:4]), .dp(1'b0));
  _02_register _02_register_2 (
    .DE(IRRI), .OE(IRO), .RST(RST_t), .D0(BUS_0), .D1(BUS_1), .D2(BUS_2), .D3(BUS_3), .CLK(CLOCK),
    .D4(BUS_4), .D5(BUS_5), .D6(BUS_6), .D7(BUS_7), .Q0(BUS_0), .Q1(BUS_1), .Q2(BUS_2), .Q3(BUS_3),
    .Q4(BUS_4), .Q5(BUS_5), .Q6(BUS_6), .Q7(BUS_7));
  Seven_Seg_Hex seven_seg_hex_8 (.d(DEBUG_IROPCODE[3:0]), .dp(1'b0));
  Seven_Seg_Hex seven_seg_hex_9 (.d({BUS_7, BUS_6, BUS_5, BUS_4}), .dp(1'b0));
  _74245 _74245_1 (
    .pin1(1'b1), .pin2(_0), .pin3(_1), .pin4(_2), .pin5(_3), .pin6(_4), .pin7(_5), .pin8(_6), .pin9(_7),
    .pin10(1'b0), .pin11(BUS_7), .pin12(BUS_6), .pin13(BUS_5), .pin14(BUS_4), .pin15(BUS_3), .pin16(BUS_2),
    .pin17(BUS_1), .pin18(BUS_0), .pin19(IOE), .pin20(1'b1));
  Seven_Seg_Hex seven_seg_hex_10 (.d({BUS_3, BUS_2, BUS_1, BUS_0}), .dp(1'b0));
  not not_3 (IOE, IO);
  not not_4 (RWE, RW);
  not not_5 (RAIE, MI);
  _02_register _02_register_3 (
    .DE(AIE), .OE(AOE), .RST(RST_t), .D0(BUS_0), .D1(BUS_1), .D2(BUS_2), .D3(BUS_3), .CLK(CLOCK), .D4(BUS_4),
    .D5(BUS_5), .D6(BUS_6), .D7(BUS_7), .Q0(BUS_0), .Q1(BUS_1), .Q2(BUS_2), .Q3(BUS_3), .Q4(BUS_4),
    .Q5(BUS_5), .Q6(BUS_6), .Q7(BUS_7));
  _07_program_counter _07_program_counter_1 (
    .PCCE(CE), .D0(BUS_0), .D1(BUS_1), .D2(BUS_2), .D3(BUS_3), .D4(BUS_4), .D5(BUS_5), .D6(BUS_6),
    .Q0(BUS_0), .Q1(BUS_1), .D7(BUS_7), .RST(RST_t_t), .CLK(CLOCK), .Q2(BUS_2), .Q3(BUS_3), .Q4(BUS_4),
    .Q5(BUS_5), .Q6(BUS_6), .Q7(BUS_7), .ERR(ERR), .PCOE(PCOE), .JMP(JMP));
  not not_6 (ROE, RO);
  not not_7 (PCOE, CO);
  LED u__7 (.in(BUS_7));
  not not_8 (JMP, JUMP);
  LED u__6 (.in(BUS_6));
  LED u__5 (.in(BUS_5));
  not not_9 (IRCI, CODEI);
  not not_10 (IRRI, RANDI);
  LED u__4 (.in(BUS_4));
  LED u__3 (.in(BUS_3));
  not not_11 (IRO, RANDO);
  LED u__2 (.in(BUS_2));
  LED u__1 (.in(BUS_1));
  not not_12 (BIE, BI);
  LED u__0 (.in(BUS_0));
  not not_13 (AIE, AI);
  not not_14 (BOE, BO);
  not not_15 (AOE, AO);
  _02_register _02_register_4 (
    .DE(BIE), .OE(BOE), .RST(RST_t), .D0(BUS_0), .D1(BUS_1), .D2(BUS_2), .D3(BUS_3), .CLK(CLOCK), .D4(BUS_4),
    .D5(BUS_5), .D6(BUS_6), .D7(BUS_7), .Q0(BUS_0), .Q1(BUS_1), .Q2(BUS_2), .Q3(BUS_3), .Q4(BUS_4),
    .Q5(BUS_5), .Q6(BUS_6), .Q7(BUS_7));
  _02_register _02_register_5 (
    .DE(RAIE), .OE(1'b0), .RST(RST_t), .D0(BUS_0), .D1(BUS_1), .D2(BUS_2), .D3(BUS_3), .CLK(CLOCK),
    .D4(BUS_4), .D5(BUS_5), .D6(BUS_6), .D7(BUS_7), .Q0(_02_register_5_q0[0]), .Q1(_02_register_5_q0[1]),
    .Q2(_02_register_5_q0[2]), .Q3(_02_register_5_q0[3]), .Q4(_02_register_5_q0[4]),
    .Q5(_02_register_5_q0[5]), .Q6(_02_register_5_q0[6]), .Q7(_02_register_5_q0[7]));
  nor nor_1 (nor_1_out, 1'b0, ~RWE, ROE);  // NOr
  RAMSinglePortSel #(.AddrBits(8), .isProgramMemory("true"), .Bits(8)) ramsingleportsel_1 (
    .A(_02_register_5_q0), .CS(~1'b0), .WE(~RWE), .OE(~ROE), .D(ramsingleportsel_1_d));
  BusSplitter #(.Bits(8)) bussplitter_1 (
    .D(ramsingleportsel_1_d), .OE(nor_1_out), .D0(BUS_0), .D1(BUS_1), .D2(BUS_2), .D3(BUS_3), .D4(BUS_4),
    .D5(BUS_5), .D6(BUS_6), .D7(BUS_7));

  // Other names for the same wires on the sheet: PCCE = CE;
  //   DEBUG_IROPRAND[7:0] = {BUS_7, BUS_6, BUS_5, BUS_4, BUS_3, BUS_2, BUS_1, BUS_0}; CLK = CLOCK

  // Notes on the sheet:
  //   CLOCK: Hz: 2
  //   contents of eeprom_1 (hex, n*v repeats v):
  //   0,0,0,0,0,0,0,0,0,0,0,0,0,0,4800,1500,4800,1480,4040,1002,0,0,0,0,0,0,0,0,0,0,4800,
  //   1500,4800,1480,4040,1008,0,0,0,0,0,0,0,0,0,0,4800,1500,4800,1480,42,0,0,0,0,0,0,0,
  //   0,0,0,0,4800,1500,4800,1480,48,0,0,0,0,0,0,0,0,0,0,0,4800,1500
  //   Input
  //   Program Counter
  //   Register A
  //   RAM
  //   Register B
endmodule
